# Fritzing sketch LightingSchematic_v1 (saved by Fritzing 0.8.7b)
breadboards: 1

parts:
  Part1 = Arduino Uno (Rev3)
  LED1 = RGB LED (com. anode, rbg) [package="5 mm [THT]"]  # not connected
  R1 = Resistor [tolerance=±5% resistance=560 package=THT]  # not connected
  R1_2 = Resistor [tolerance=±5% resistance=560 package="1206 [SMD]"]  # not connected
  R2 = Resistor [tolerance=±5% resistance=560 package="1206 [SMD]"]  # not connected
  R3 = Photocell (LDR) [package=THT]
  R4 = Resistor [tolerance=±5% resistance=10k package=THT]

nets:
  N1: Part1.A0, R3.pin_0, R4.Pin_1
  N2: Part1.5V, R4.Pin_0
  N3: Part1.GND, R3.pin_1
